# Fritzing sketch MotorArduino (saved by Fritzing 0.9.5d)
breadboards: 1

parts:
  IC1 = L293D [package=THT]
  Bauteil1 = Arduino Uno (Rev3)
  C1 = Electrolytic Capacitor [capacitance=100µF package="100 mil [THT, electrolytic]"]
  C2 = Ceramic Capacitor [capacitance=100nF package="100 mil [THT, multilayer]"]
  U1 = DIODE-ZENER [package=diode-zener]
  U2 = DIODE-ZENER [package=diode-zener]  # not connected
  U3 = DIODE-ZENER [package=diode-zener]
  U4 = DIODE-ZENER [package=diode-zener]
  M1 = DC Motor
  Power_plug1 = Power plug

nets:
  N1: IC1.Enable_1, Bauteil1.D5_PWM
  N2: IC1.In_1, Bauteil1.D4
  N3: IC1.Out_1_(_Controlled_by_Enable_1_), U1.C, M1.pin_2
  N4: IC1.0V, Bauteil1.GND
  N5: IC1.Out_2_(_Controlled_by_Enable_1_), M1.pin_1
  N6: IC1.In_2, Bauteil1.D3_PWM
  N7: IC1.+Vmotor, Bauteil1.5V
  N8: C1.-, C2.0, Power_plug1.GND
  N9: C1.+, C2.1, U3.C, U4.C, Power_plug1.VCC
