# Fritzing sketch MotorArduino_Treiber (saved by Fritzing 0.9.5d)

parts:
  Bauteil1 = Arduino Uno (Rev3)
  S1 = H-Bridge with L298N
  M1 = DC Motor
  M2 = DC Motor

nets:
  N1: Bauteil1.D8, S1.IN2
  N2: Bauteil1.D9_PWM, S1.IN1
  N3: Bauteil1.D10_PWM/SS, S1.ENA
  N4: Bauteil1.D5_PWM, S1.ENB
  N5: Bauteil1.D6_PWM, S1.IN4
  N6: Bauteil1.D7, S1.IN3
  GND: Bauteil1.GND, S1.GND
  VIN: Bauteil1.VIN, S1.12V
  N7: S1.M1-01, M2.pin_2
  N8: S1.M1-02, M2.pin_1
  N9: S1.M2-01, M1.pin_2
  N10: S1.M2-02, M1.pin_1

notes:
  Spannungsversorgung

custom parts:
  H-Bridge with L298N: h-bridge
