# Fritzing sketch Schaltplan (saved by Fritzing 0.9.5d)
breadboards: 1

parts:
  Bauteil2 = Arduino Uno (Rev3) - ICSP
  RE1 = KY-040 Rotary encoder [package=THT]
  L298N1 = L298N DC motor driver
  LCD2 = LCD screen
  LCM1602_IIC1 = LCM1602 IIC [part_number="LCM1602 IIC" chip_label="LCM1602 IIC" package="DIP (Dual Inline) [THT]"]
  Mod1 = KY-022 Infrared Receiver Module [package="Breakout board"]
  M1 = DC Motor
  M2 = DC Motor
  M3 = Dagu DGServo 9g (End View) [part_number=RS001B]

nets:
  N1: Bauteil2.ICSP_MISO, Bauteil2.D12/MISO, L298N1.IN1
  N2: Bauteil2.D8, L298N1.IN2
  N3: Bauteil2.D9_PWM, Mod1.S
  N4: Bauteil2.D10_PWM/SS, M3.pulse
  N5: Bauteil2.D11_PWM/MOSI, L298N1.ENA
  N6: Bauteil2.A4/SDA, LCM1602_IIC1.SDA
  N7: Bauteil2.A5/SCL, LCM1602_IIC1.SCL
  N8: Bauteil2.D2, RE1.CLK
  N9: Bauteil2.D3_PWM, RE1.DT
  N10: Bauteil2.D4, RE1.SW
  N11: Bauteil2.D5_PWM, L298N1.ENB
  N12: Bauteil2.D6_PWM, L298N1.IN4
  N13: Bauteil2.D7, L298N1.IN3
  GND: Bauteil2.GND, L298N1.GND
  VIN: Bauteil2.VIN, L298N1.5V
  GND_2: RE1.GND, LCM1602_IIC1.GND, Mod1.-, M3.gnd
  VCC: RE1.Vcc, LCM1602_IIC1.VCC, Mod1.Vin, M3.vcc
  N14: L298N1.OUT1, M2.pin_1
  N15: L298N1.OUT2, M2.pin_2
  N16: L298N1.OUT3, M1.pin_2
  N17: L298N1.OUT4, M1.pin_1
  VSS: LCD2.VSS, LCM1602_IIC1.VSS
  VDD: LCD2.VDD, LCM1602_IIC1.VDD
  N18: LCD2.V0, LCM1602_IIC1.V0
  N19: LCD2.RS, LCM1602_IIC1.RS
  N20: LCD2.R/W, LCM1602_IIC1.RW
  N21: LCD2.E, LCM1602_IIC1.E
  N22: LCD2.DB0, LCM1602_IIC1.D0
  N23: LCD2.DB1, LCM1602_IIC1.D1
  N24: LCD2.DB2, LCM1602_IIC1.D2
  N25: LCD2.DB3, LCM1602_IIC1.D3
  N26: LCD2.DB4, LCM1602_IIC1.D4
  N27: LCD2.DB5, LCM1602_IIC1.D5
  N28: LCD2.DB6, LCM1602_IIC1.D6
  N29: LCD2.DB7, LCM1602_IIC1.D7
  N30: LCD2.LED+, LCM1602_IIC1.A
  N31: LCD2.LED-, LCM1602_IIC1.K
  N32: LCM1602_IIC1.LED_A, LCM1602_IIC1.LED_B

notes:
  Spannungsversorgung

custom parts:
  KY-040 Rotary encoder: KY-040 Rotary Encoder with switch on breakout borad from AZ Delivery
  L298N DC motor driver: 2x DC motor driver with 78M05 positive voltage regulator (7..35 V) L298N: max 46 V, 2 A Set 5 V Enable jumper to enable 5 V regultor (needed for the L298N) and +5 V output at screw terminal or supply external +5 V at screw terminal Set ENA and/or ENB to +5 V to enable motor permanently or supply ENA and/or ENB with PWM signal IN1 and IN2 set rotation directory for motor A (OUT1/OUT2) IN2 and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
  LCM1602 IIC: I2C-Module to use a 1602 or 2004 LCD on with the wire.h libory Serial LCD Modul
  KY-022 Infrared Receiver Module: KY-022 IR receiver module, reacts to 38kHz infrared light.
